// Logisim project 20 Bit CPU.circ as structural Verilog: 7 circuits, main circuit main
module main (
  input  [4:0] in_1,
  input  in_2,
  input  in_3,
  output [3:0] out_4,
  output [3:0] out_5,
  output out_6,
  output [2:0] out_7,
  output [1:0] out_8,
  output [19:0] out_9,
  output [19:0] out_10,
  output [19:0] out_11,
  output [19:0] out_12
);

  wire and_1_out, button_1_out, button_2_out, CLK_out, control_unit_1_alu_src, control_unit_1_branch,
       control_unit_1_jump, control_unit_1_mem_read, control_unit_1_mem_to_reg, control_unit_1_mem_write,
       control_unit_1_reg_dest, control_unit_1_reg_write, n20_bit_minimize_1_out_7, n20_bit_minimize_1_out_8,
       or_1_out;
  wire [3:0] multiplexer_1_out;
  wire [19:0] adder_1_out, adder_2_out, bit_extender_1_out, bit_extender_2_out, multiplexer_2_out,
       multiplexer_3_out, multiplexer_4_out, ram_1_data, register_1_q, rom_1_data;

  Button button_1 (.out(button_1_out));
  Register #(.width(20)) register_1 (
    .D(multiplexer_4_out), .Q(register_1_q), .clk(CLK_out), .clr(button_1_out));  // open: en
  Adder #(.width(20)) adder_1 (.a(20'h1), .b(register_1_q), .out(adder_1_out));  // open: cin, cout
  ROM #(.addrWidth(20), .dataWidth(20)) rom_1 (
    .addr(register_1_q), .data({rom_1_data[19:16], out_4, out_5, rom_1_data[7:0]}));  // open: sel
  Multiplexer #(.width(4), .enable("false")) multiplexer_1 (
    .in0(out_5), .in1(rom_1_data[7:4]), .out(multiplexer_1_out), .sel(control_unit_1_reg_dest));
  Control_Unit control_unit_1 (
    .in_1(rom_1_data[19:16]), .Reg_Dest(control_unit_1_reg_dest), .Reg_Write(control_unit_1_reg_write),
    .Alu_Op(out_8), .Alu_Src(control_unit_1_alu_src), .Mem_Write(control_unit_1_mem_write),
    .Mem_Read(control_unit_1_mem_read), .Mem_To_Reg(control_unit_1_mem_to_reg),
    .Branch(control_unit_1_branch), .Jump(control_unit_1_jump));
  assign bit_extender_1_out = {{4{1'b0}}, {out_4, out_5, rom_1_data[7:0]}};  // Bit_Extender bit_extender_1
  assign bit_extender_2_out = {{12{1'b0}}, rom_1_data[7:0]};  // Bit_Extender bit_extender_2
  _20_Bit_Register_File u_20_bit_register_file_1 (
    .Data_Write(out_11), .Read_Data_1(out_9), .Read_Register_1(out_4), .Read_Data_2(out_10),
    .Read_Register_2(out_5), .Write_Register(multiplexer_1_out), .Write_Control(control_unit_1_reg_write),
    .Clock(CLK_out));  // open: Clear
  Multiplexer #(.width(20), .enable("false")) multiplexer_2 (
    .in0(out_10), .in1(bit_extender_2_out), .out(multiplexer_2_out), .sel(control_unit_1_alu_src));
  Shifter #(.width(20)) shifter_1 (.\dist (in_1));  // open: in, out
  Adder #(.width(20)) adder_2 (.a(adder_1_out), .b(bit_extender_2_out), .out(adder_2_out));  // open: cin, cout
  _20_Bit_Minimize u_20_bit_minimize_1 (
    .Cin(in_2), .Cout(out_6), .out_6(out_12), .A(out_9), .B(multiplexer_2_out),
    .out_7(n20_bit_minimize_1_out_7), .out_8(n20_bit_minimize_1_out_8), .in_4(out_7));
  or or_1 (or_1_out, n20_bit_minimize_1_out_7, n20_bit_minimize_1_out_8);
  ALU_Control alu_control_1 (.func(rom_1_data[3:0]), .ALU_op(out_8), .out_4(out_7), .opcode(rom_1_data[19:16]));
  and and_1 (and_1_out, control_unit_1_branch, or_1_out);
  Multiplexer #(.width(20), .enable("false")) multiplexer_3 (
    .in0(adder_1_out), .in1(adder_2_out), .out(multiplexer_3_out), .sel(and_1_out));
  Clock CLK (.out(CLK_out));
  Multiplexer #(.width(20), .enable("false")) multiplexer_4 (
    .in0(multiplexer_3_out), .in1(bit_extender_1_out), .out(multiplexer_4_out), .sel(control_unit_1_jump));
  RAM #(.addrWidth(20), .dataWidth(20), .bus("separate")) ram_1 (
    .addr(out_12), .din(out_10), .data(ram_1_data), .str(control_unit_1_mem_write), .clk(CLK_out),
    .ld(control_unit_1_mem_read), .clr(button_2_out));  // open: sel
  Button button_2 (.out(button_2_out));
  Multiplexer #(.width(20), .enable("false")) multiplexer_5 (
    .in0(out_12), .in1(ram_1_data), .out(out_11), .sel(control_unit_1_mem_to_reg));

  // Notes on the sheet:
  //   func
  //   rd
  //   rt
  //   rs
  //   opcode
endmodule

module _1bit_ALU (
  input  A,
  input  B,
  input  Cin,
  input  [2:0] in_4,
  output Cout,
  output out_6,
  output out_7,
  output out_8
);

  wire adder_1_out, and_1_out, comparator_1_lt, nor_1_out, or_1_out, shifter_1_out, shifter_2_out,
       subtractor_1_out;

  // NOT_Gate not_1 has open pins: in=B, out=open
  Adder #(.width(1)) adder_1 (.a(A), .b(B), .out(adder_1_out), .cin(Cin), .cout(Cout));
  Subtractor #(.width(1)) subtractor_1 (.a(A), .b(B), .out(subtractor_1_out));  // open: bin, bout
  Shifter #(.width(1)) shifter_1 (.in(A), .\dist (1'b1), .out(shifter_1_out));
  or or_1 (or_1_out, A, B);
  nor nor_1 (nor_1_out, A, B);
  Comparator #(.width(1)) comparator_1 (.a(A), .b(B), .eq(out_7), .lt(comparator_1_lt));  // open: gt
  and and_1 (and_1_out, A, B);
  Shifter #(.width(1), .shift("lr")) shifter_2 (.in(A), .\dist (1'b1), .out(shifter_2_out));
  Multiplexer #(.select(3), .enable("false")) multiplexer_1 (
    .in0(adder_1_out), .in1(shifter_1_out), .in2(or_1_out), .in3(subtractor_1_out), .in4(nor_1_out),
    .in5(comparator_1_lt), .in6(and_1_out), .in7(shifter_2_out), .out(out_6), .sel(in_4));
  not not_2 (out_8, out_7);
endmodule

module _20_Bit_Register_File (
  input  [19:0] Data_Write,
  input  [3:0] Read_Register_1,
  input  [3:0] Write_Register,
  input  [3:0] Read_Register_2,
  input  Write_Control,
  input  Clock,
  input  Clear,
  output [19:0] Read_Data_1,
  output [19:0] Read_Data_2
);

  wire and_1_out, and_2_out, and_3_out, and_4_out, and_5_out, and_6_out, and_7_out, and_8_out, and_9_out,
       and_10_out, and_11_out, and_12_out, and_13_out, and_14_out, and_15_out, and_16_out, decoder_1_out0,
       decoder_1_out1, decoder_1_out2, decoder_1_out3, decoder_1_out4, decoder_1_out5, decoder_1_out6,
       decoder_1_out7, decoder_1_out8, decoder_1_out9, decoder_1_out10, decoder_1_out11, decoder_1_out12,
       decoder_1_out13, decoder_1_out14, decoder_1_out15;
  wire [19:0] _0_q, _1_q, _2_q, _3_q, _4_q, _5_q, _6_q, _7_q, _8_q, _9_q, _10_q, _11_q, _12_q, _13_q, _14_q,
       _15_q;

  Decoder #(.select(4), .enable("false")) decoder_1 (
    .out0(decoder_1_out0), .out1(decoder_1_out1), .out2(decoder_1_out2), .out3(decoder_1_out3),
    .out4(decoder_1_out4), .out5(decoder_1_out5), .out6(decoder_1_out6), .out7(decoder_1_out7),
    .out8(decoder_1_out8), .out9(decoder_1_out9), .out10(decoder_1_out10), .out11(decoder_1_out11),
    .out12(decoder_1_out12), .out13(decoder_1_out13), .out14(decoder_1_out14), .out15(decoder_1_out15),
    .sel(Write_Register));
  and and_1 (and_1_out, decoder_1_out0, Write_Control);
  and and_2 (and_2_out, decoder_1_out1, Write_Control);
  and and_3 (and_3_out, decoder_1_out2, Write_Control);
  and and_4 (and_4_out, decoder_1_out3, Write_Control);
  and and_5 (and_5_out, decoder_1_out4, Write_Control);
  and and_6 (and_6_out, decoder_1_out5, Write_Control);
  and and_7 (and_7_out, decoder_1_out6, Write_Control);
  and and_8 (and_8_out, decoder_1_out7, Write_Control);
  Register #(.width(20)) _0 (.D(Data_Write), .en(and_1_out), .Q(_0_q), .clk(Clock), .clr(Clear));
  Register #(.width(20)) _1 (.D(Data_Write), .en(and_2_out), .Q(_1_q), .clk(Clock), .clr(Clear));
  Register #(.width(20)) _2 (.D(Data_Write), .en(and_3_out), .Q(_2_q), .clk(Clock), .clr(Clear));
  Register #(.width(20)) _3 (.D(Data_Write), .en(and_4_out), .Q(_3_q), .clk(Clock), .clr(Clear));
  Register #(.width(20)) _4 (.D(Data_Write), .en(and_5_out), .Q(_4_q), .clk(Clock), .clr(Clear));
  Register #(.width(20)) _5 (.D(Data_Write), .en(and_6_out), .Q(_5_q), .clk(Clock), .clr(Clear));
  Register #(.width(20)) _6 (.D(Data_Write), .en(and_7_out), .Q(_6_q), .clk(Clock), .clr(Clear));
  Register #(.width(20)) _7 (.D(Data_Write), .en(and_8_out), .Q(_7_q), .clk(Clock), .clr(Clear));
  and and_9 (and_9_out, decoder_1_out8, Write_Control);
  and and_10 (and_10_out, decoder_1_out9, Write_Control);
  and and_11 (and_11_out, decoder_1_out10, Write_Control);
  and and_12 (and_12_out, decoder_1_out11, Write_Control);
  and and_13 (and_13_out, decoder_1_out12, Write_Control);
  and and_14 (and_14_out, decoder_1_out13, Write_Control);
  and and_15 (and_15_out, decoder_1_out14, Write_Control);
  and and_16 (and_16_out, decoder_1_out15, Write_Control);
  Register #(.width(20)) _8 (.D(Data_Write), .en(and_9_out), .Q(_8_q), .clk(Clock), .clr(Clear));
  Register #(.width(20)) _9 (.en(and_10_out), .Q(_9_q), .clk(Clock), .clr(Clear));  // open: D
  Register #(.width(20)) _10 (.D(Data_Write), .en(and_11_out), .Q(_10_q), .clk(Clock), .clr(Clear));
  Register #(.width(20)) _11 (.D(Data_Write), .en(and_12_out), .Q(_11_q), .clk(Clock), .clr(Clear));
  Register #(.width(20)) _12 (.D(Data_Write), .en(and_13_out), .Q(_12_q), .clk(Clock), .clr(Clear));
  Register #(.width(20)) _13 (.D(Data_Write), .en(and_14_out), .Q(_13_q), .clk(Clock), .clr(Clear));
  Register #(.width(20)) _14 (.D(Data_Write), .en(and_15_out), .Q(_14_q), .clk(Clock), .clr(Clear));
  Register #(.width(20)) _15 (.D(Data_Write), .en(and_16_out), .Q(_15_q), .clk(Clock), .clr(Clear));
  Multiplexer #(.select(4), .width(20), .enable("false")) multiplexer_1 (
    .in0(_0_q), .in1(_1_q), .in2(_2_q), .in3(_3_q), .in4(_4_q), .in5(_5_q), .in6(_6_q), .in7(_7_q),
    .in8(_8_q), .in9(_9_q), .in10(_10_q), .in11(_11_q), .in12(_12_q), .in13(_13_q), .in14(_14_q),
    .in15(_15_q), .out(Read_Data_1), .sel(Read_Register_1));
  Multiplexer #(.select(4), .width(20), .enable("false")) multiplexer_2 (
    .in0(_0_q), .in1(_1_q), .in2(_2_q), .in3(_3_q), .in4(_4_q), .in5(_5_q), .in6(_6_q), .in7(_7_q),
    .in8(_8_q), .in9(_9_q), .in10(_10_q), .in11(_11_q), .in12(_12_q), .in13(_13_q), .in14(_14_q),
    .in15(_15_q), .out(Read_Data_2), .sel(Read_Register_2));

  // Notes on the sheet:
  //   Md Abu Bokar
  //   2222977642
endmodule

module _20_Bit_ALU (
  input  Cin,
  input  [19:0] A,
  input  [19:0] B,
  input  [2:0] ALU_opt,
  output [19:0] out_5,
  output Not_Zero_Flag,
  output Zero_Flag,
  output out_8
);

  wire _0_cout, _1_cout, _2_cout, _3_cout, _4_cout, _5_cout, _6_cout, _7_cout, _8_cout, _9_cout, _10_cout,
       _11_cout, _12_cout, _13_cout, _14_cout, _15_cout, _16_cout, _17_cout, _18_cout;

  _1bit_ALU _0 (.A(A[0]), .B(B[0]), .Cin(Cin), .Cout(_0_cout), .out_6(out_5[0]), .in_4(ALU_opt));  // open: out_7, out_8
  _1bit_ALU _19 (
    .A(A[19]), .B(B[19]), .Cin(_18_cout), .Cout(out_8), .out_6(out_5[19]), .in_4(ALU_opt));  // open: out_7, out_8
  _1bit_ALU _1 (
    .A(A[1]), .B(B[1]), .Cin(_0_cout), .Cout(_1_cout), .out_6(out_5[1]), .in_4(ALU_opt));  // open: out_7, out_8
  _1bit_ALU _18 (
    .A(A[18]), .B(B[18]), .Cin(_17_cout), .Cout(_18_cout), .out_6(out_5[18]), .in_4(ALU_opt));  // open: out_7, out_8
  _1bit_ALU _2 (
    .A(A[2]), .B(B[2]), .Cin(_1_cout), .Cout(_2_cout), .out_6(out_5[2]), .in_4(ALU_opt));  // open: out_7, out_8
  _1bit_ALU _17 (
    .A(A[17]), .B(B[17]), .Cin(_16_cout), .Cout(_17_cout), .out_6(out_5[17]), .in_4(ALU_opt));  // open: out_7, out_8
  _1bit_ALU _3 (
    .A(A[3]), .B(B[3]), .Cin(_2_cout), .Cout(_3_cout), .out_6(out_5[3]), .in_4(ALU_opt));  // open: out_7, out_8
  _1bit_ALU _16 (
    .A(A[16]), .B(B[16]), .Cin(_15_cout), .Cout(_16_cout), .out_6(out_5[16]), .in_4(ALU_opt));  // open: out_7, out_8
  _1bit_ALU _4 (
    .A(A[4]), .B(B[4]), .Cin(_3_cout), .Cout(_4_cout), .out_6(out_5[4]), .in_4(ALU_opt));  // open: out_7, out_8
  _1bit_ALU _15 (
    .A(A[15]), .B(B[15]), .Cin(_14_cout), .Cout(_15_cout), .out_6(out_5[15]), .in_4(ALU_opt));  // open: out_7, out_8
  _1bit_ALU _5 (
    .A(A[5]), .B(B[5]), .Cin(_4_cout), .Cout(_5_cout), .out_6(out_5[5]), .in_4(ALU_opt));  // open: out_7, out_8
  _1bit_ALU _14 (
    .A(A[14]), .B(B[14]), .Cin(_13_cout), .Cout(_14_cout), .out_6(out_5[14]), .in_4(ALU_opt));  // open: out_7, out_8
  _1bit_ALU _6 (
    .A(A[6]), .B(B[6]), .Cin(_5_cout), .Cout(_6_cout), .out_6(out_5[6]), .in_4(ALU_opt));  // open: out_7, out_8
  _1bit_ALU _13 (
    .A(A[13]), .B(B[13]), .Cin(_12_cout), .Cout(_13_cout), .out_6(out_5[13]), .in_4(ALU_opt));  // open: out_7, out_8
  _1bit_ALU _7 (
    .A(A[7]), .B(B[7]), .Cin(_6_cout), .Cout(_7_cout), .out_6(out_5[7]), .in_4(ALU_opt));  // open: out_7, out_8
  _1bit_ALU _12 (
    .A(A[12]), .B(B[12]), .Cin(_11_cout), .Cout(_12_cout), .out_6(out_5[12]), .in_4(ALU_opt));  // open: out_7, out_8
  _1bit_ALU _8 (
    .A(A[8]), .B(B[8]), .Cin(_7_cout), .Cout(_8_cout), .out_6(out_5[8]), .in_4(ALU_opt));  // open: out_7, out_8
  _1bit_ALU _11 (
    .A(A[11]), .B(B[11]), .Cin(_10_cout), .Cout(_11_cout), .out_6(out_5[11]), .in_4(ALU_opt));  // open: out_7, out_8
  _1bit_ALU _9 (
    .A(A[9]), .B(B[9]), .Cin(_8_cout), .Cout(_9_cout), .out_6(out_5[9]), .in_4(ALU_opt));  // open: out_7, out_8
  _1bit_ALU _10 (
    .A(A[10]), .B(B[10]), .Cin(_9_cout), .Cout(_10_cout), .out_6(out_5[10]), .in_4(ALU_opt));  // open: out_7, out_8
  not not_1 (Not_Zero_Flag, Zero_Flag);
  nor nor_1 (Zero_Flag, out_5[0], out_5[1], out_5[2], out_5[3], out_5[4], out_5[5], out_5[6], out_5[7], out_5[8], out_5[9], out_5[10], out_5[11], out_5[12], out_5[13], out_5[14], out_5[15], out_5[16], out_5[17], out_5[18], out_5[19]);

  // Notes on the sheet:
  //   Md Abu Bokar
  //   2222977642
endmodule

module _20_Bit_Minimize (
  input  [19:0] A,
  input  [19:0] B,
  input  Cin,
  input  [2:0] in_4,
  output Cout,
  output [19:0] out_6,
  output out_7,
  output out_8
);

  wire comparator_1_lt;
  wire [4:0] bit_extender_1_out, bit_extender_2_out;
  wire [19:0] adder_1_out, and_1_out, bit_extender_3_out, nor_1_out, or_1_out, shifter_1_out, shifter_2_out,
       subtractor_1_out;

  // NOT_Gate not_1 has open pins: in=B, out=open
  assign bit_extender_1_out = {{4{1'b0}}, 1'b1};  // Bit_Extender bit_extender_1
  assign bit_extender_2_out = {{4{1'b0}}, 1'b1};  // Bit_Extender bit_extender_2
  Adder #(.width(20)) adder_1 (.a(A), .b(B), .out(adder_1_out), .cin(Cin), .cout(Cout));
  Subtractor #(.width(20)) subtractor_1 (.a(A), .b(B), .out(subtractor_1_out));  // open: bin, bout
  Shifter #(.width(20)) shifter_1 (.in(A), .\dist (bit_extender_1_out), .out(shifter_1_out));
  assign or_1_out = A | B;  // OR_Gate or_1, 20 bits wide
  assign nor_1_out = ~(A | B);  // NOR_Gate nor_1, 20 bits wide
  Comparator #(.width(20)) comparator_1 (.a(A), .b(B), .eq(out_7), .lt(comparator_1_lt));  // open: gt
  assign and_1_out = A & B;  // AND_Gate and_1, 20 bits wide
  Shifter #(.width(20), .shift("lr")) shifter_2 (.in(A), .\dist (bit_extender_2_out), .out(shifter_2_out));
  assign bit_extender_3_out = {{19{1'b0}}, comparator_1_lt};  // Bit_Extender bit_extender_3
  Multiplexer #(.select(3), .width(20), .enable("false")) multiplexer_1 (
    .in0(adder_1_out), .in1(shifter_1_out), .in2(or_1_out), .in3(subtractor_1_out), .in4(nor_1_out),
    .in5(bit_extender_3_out), .in6(and_1_out), .in7(shifter_2_out), .out(out_6), .sel(in_4));
  not not_2 (out_8, out_7);
endmodule

module Control_Unit (
  input  [3:0] in_1,
  output Reg_Dest,
  output Reg_Write,
  output Alu_Src,
  output Mem_Write,
  output Mem_Read,
  output Mem_To_Reg,
  output Branch,
  output Jump,
  output [1:0] Alu_Op
);

  wire decoder_1_out3, decoder_1_out4;

  Decoder #(.select(4), .enable("false")) decoder_1 (
    .out0(Alu_Op[1]), .out1(Alu_Op[0]), .out2(Mem_Write), .out3(decoder_1_out3), .out4(decoder_1_out4),
    .out5(Jump), .out6(Mem_Read), .sel(in_1));  // open: out7, out8, out9, out10, out11, out12, out13, out14, out15
  or or_1 (Reg_Write, Alu_Op[1], decoder_1_out4, Mem_Read);
  or or_2 (Alu_Src, Mem_Write, decoder_1_out4, Mem_Read);
  or or_3 (Branch, Alu_Op[0], decoder_1_out3, Jump);

  assign Mem_To_Reg = Mem_Read;
  assign Reg_Dest = Alu_Op[1];
endmodule

module ALU_Control (
  input  [3:0] func,
  input  [3:0] opcode,
  input  [1:0] ALU_op,
  output [2:0] out_4
);

  wire and_out, decoder_1_out0, decoder_1_out1, decoder_1_out2, decoder_1_out3, decoder_1_out4,
       decoder_1_out5, decoder_1_out6, decoder_1_out7, decoder_1_out8, decoder_2_out0, decoder_2_out1,
       decoder_2_out2, decoder_2_out3, decoder_2_out4, decoder_2_out5, decoder_2_out6, decoder_2_out7,
       decoder_2_out8, decoder_3_out1, decoder_3_out2, nor_out, or_out, sll_out, slt_out, srl_out, sub_out;

  Decoder #(.select(4), .enable("false")) decoder_1 (
    .out0(decoder_1_out0), .out1(decoder_1_out1), .out2(decoder_1_out2), .out3(decoder_1_out3),
    .out4(decoder_1_out4), .out5(decoder_1_out5), .out6(decoder_1_out6), .out7(decoder_1_out7),
    .out8(decoder_1_out8), .sel(func));  // open: out9, out10, out11, out12, out13, out14, out15
  Decoder #(.select(4), .enable("false")) decoder_2 (
    .out0(decoder_2_out0), .out1(decoder_2_out1), .out2(decoder_2_out2), .out3(decoder_2_out3),
    .out4(decoder_2_out4), .out5(decoder_2_out5), .out6(decoder_2_out6), .out7(decoder_2_out7),
    .out8(decoder_2_out8), .sel(opcode));  // open: out9, out10, out11, out12, out13, out14, out15
  Decoder #(.select(2), .enable("false")) decoder_3 (
    .out1(decoder_3_out1), .out2(decoder_3_out2), .sel(ALU_op));  // open: out0, out3
  // AND_Gate add has open pins: in0=decoder_3_out2, in1=decoder_2_out0, in2=decoder_1_out0, out=open
  and sll (sll_out, decoder_3_out2, decoder_2_out0, decoder_1_out1);
  or _2 (out_4[2], srl_out, and_out, slt_out, nor_out);
  and \or  (or_out, decoder_3_out2, decoder_2_out0, decoder_1_out2);
  and \nor  (nor_out, decoder_3_out2, decoder_2_out0, decoder_1_out4);
  and sub (sub_out, decoder_3_out2, decoder_2_out0, decoder_1_out3);
  or _1 (out_4[1], decoder_3_out1, srl_out, and_out, sub_out, or_out);
  and slt (slt_out, decoder_3_out2, decoder_2_out0, decoder_1_out5);
  or _0 (out_4[0], decoder_3_out1, srl_out, slt_out, sub_out, sll_out);
  and \and  (and_out, decoder_3_out2, decoder_2_out0, decoder_1_out6);
  and srl (srl_out, decoder_3_out2, decoder_2_out0, decoder_1_out8);
endmodule
